// Logisim project address_decode.circ as structural Verilog: 1 circuit, main circuit main
module main (
);

  wire A0, A1, A2, A3, A4, A5, A6, A7, A8, A9, A10, A11, A12, A13, A13OR12, A14, A15, and_1_out, and_2_out,
       and_3_out, and_4_out, and_5_out, and_7_out, and_8_out, and_9_out, and_10_out, and_11_out, and_12_out,
       and_13_out, and_14_out, and_15_out, and_16_out, B1, B2, BB, BSS, C006, C6XX, C007, C030, CLK,
       CS_CPUBUS, CS_DEVICE, CS_RAM, CS_ROM, CXXX, decoder_1_out0, decoder_1_out3, decoder_1_out5,
       decoder_1_out6, decoder_1_out8, decoder_1_out14, decoder_2_out0, decoder_2_out1, decoder_2_out2,
       decoder_2_out3, decoder_2_out4, decoder_2_out5, decoder_2_out6, decoder_2_out7, decoder_2_out8,
       decoder_2_out9, decoder_2_out10, decoder_2_out11, decoder_2_out12, decoder_2_out13, decoder_2_out14,
       decoder_2_out15, DEV, DISKSS, DXXX, FF, FULLMODE, GFXMODE, GFXSS, HIRES, JOYSS, KBD, LORES, LOW0,
       MIXMODE, nand_2_out, nand_4_out, nand_6_out, nand_7_out, nand_8_out, nand_9_out, nand_10_out,
       nand_11_out, nand_17_out, nand_19_out, nand_24_out, not_1_out, not_2_out, not_25_out, not_26_out,
       not_27_out, not_28_out, not_29_out, not_30_out, not_31_out, not_32_out, not_33_out, not_34_out,
       not_35_out, NOWRITE, OE, or_1_out, or_2_out, or_9_out, or_13_out, or_16_out, or_19_out, or_20_out,
       or_21_out, or_22_out, or_23_out, or_24_out, or_25_out, or_26_out, or_27_out, or_28_out, or_29_out,
       or_30_out, or_31_out, or_32_out, or_33_out, or_34_out, or_35_out, or_37_out, or_38_out, PAGE1, PAGE2,
       PHI2, RAM, RAMREAD, RAMWRITE, ROM, ROMREAD, RW, SS, TXTMODE, VIDBUS, VIDENABLE, WE, x0, x00, x000, x1,
       x2, x3, x4, x5, x6, x7, x8, x9, x30, x50, x60, x80, xA, xB, xE0;

  or or_1 (or_1_out, A11, A10);
  or or_2 (or_2_out, A9, A8);
  not not_1 (not_1_out, A13);
  not not_2 (not_2_out, A12);
  or or_3 (x000, or_1_out, or_2_out);
  or or_4 (LOW0, x00, x0);
  and and_1 (and_1_out, A15, A14);
  and and_2 (and_2_out, not_2_out, not_1_out);
  and and_3 (and_3_out, not_1_out, A12);
  Decoder #(.select(4)) decoder_1 (
    .out0(decoder_1_out0), .out3(decoder_1_out3), .out5(decoder_1_out5), .out6(decoder_1_out6),
    .out8(decoder_1_out8), .out14(decoder_1_out14), .sel({A7, A6, A5, A4}));  // open: out1, out2, out4, out7, out9, out10, out11, out12, out13, out15, en
  not not_3 (x00, decoder_1_out0);
  not not_4 (x30, decoder_1_out3);
  not not_5 (x50, decoder_1_out5);
  not not_6 (x60, decoder_1_out6);
  Decoder #(.select(4)) decoder_2 (
    .out0(decoder_2_out0), .out1(decoder_2_out1), .out2(decoder_2_out2), .out3(decoder_2_out3),
    .out4(decoder_2_out4), .out5(decoder_2_out5), .out6(decoder_2_out6), .out7(decoder_2_out7),
    .out8(decoder_2_out8), .out9(decoder_2_out9), .out10(decoder_2_out10), .out11(decoder_2_out11),
    .out12(decoder_2_out12), .out13(decoder_2_out13), .out14(decoder_2_out14), .out15(decoder_2_out15),
    .sel({A3, A2, A1, A0}));  // open: en
  not not_7 (x0, decoder_2_out0);
  not not_8 (x1, decoder_2_out1);
  not not_9 (x2, decoder_2_out2);
  not not_10 (x3, decoder_2_out3);
  not not_11 (x4, decoder_2_out4);
  not not_12 (x5, decoder_2_out5);
  not not_13 (x6, decoder_2_out6);
  or or_5 (SS, CXXX, x000);
  Hex_Digit_Display hex_digit_display_1 (.value({A15, A14, A13, A12}));  // open: dp
  DipSwitch #(.number(16)) dipswitch_1 (
    .sw1(A15), .sw2(A14), .sw3(A13), .sw4(A12), .sw5(A11), .sw6(A10), .sw7(A9), .sw8(A8), .sw9(A7),
    .sw10(A6), .sw11(A5), .sw12(A4), .sw13(A3), .sw14(A2), .sw15(A1), .sw16(A0));
  nand nand_1 (CXXX, and_1_out, and_2_out);
  not not_14 (x80, decoder_1_out8);
  not not_15 (xE0, decoder_1_out14);
  not not_16 (x7, decoder_2_out7);
  not not_17 (x8, decoder_2_out8);
  not not_18 (x9, decoder_2_out9);
  not not_19 (xA, decoder_2_out10);
  not not_20 (xB, decoder_2_out11);
  // NOT_Gate not_21 has open pins: in=decoder_2_out12, out=open
  // NOT_Gate not_22 has open pins: in=decoder_2_out13, out=open
  // NOT_Gate not_23 has open pins: in=decoder_2_out14, out=open
  or or_6 (C007, x7, or_9_out);
  Hex_Digit_Display hex_digit_display_2 (.value({A11, A10, A9, A8}));  // open: dp
  Hex_Digit_Display hex_digit_display_3 (.value({A7, A6, A5, A4}));  // open: dp
  nand nand_2 (nand_2_out, A10, A9);
  // NOT_Gate not_24 has open pins: in=decoder_2_out15, out=open
  or or_7 (GFXSS, SS, x50);
  or or_8 (C006, or_9_out, x6);
  or or_9 (or_9_out, SS, x00);
  Hex_Digit_Display hex_digit_display_4 (.value({A3, A2, A1, A0}));  // open: dp
  nand nand_3 (DXXX, and_1_out, and_3_out);
  or or_10 (C6XX, nand_2_out, CXXX);
  or or_11 (BSS, SS, x80);
  or or_12 (C030, x0, or_13_out);
  or or_13 (or_13_out, SS, x30);
  nand nand_4 (nand_4_out, JOYSS, KBD);
  or or_14 (JOYSS, SS, x60);
  LED u_dev (.in(DEV));
  or or_15 (DEV, nand_4_out, or_19_out);
  or or_16 (or_16_out, nand_6_out, or_20_out);
  or or_17 (A13OR12, A13, A12);
  Clock clock_1 (.out(CLK));
  or or_18 (DISKSS, SS, xE0);
  or or_19 (or_19_out, or_16_out, not_25_out);
  not not_25 (not_25_out, C6XX);
  or or_20 (or_20_out, A13OR12, A11);
  LED u_ram (.in(RAM));
  nand nand_5 (RAM, DEV, ROM);
  and and_4 (and_4_out, or_21_out, or_23_out);
  or or_21 (or_21_out, C6XX, A11);
  or or_22 (or_22_out, nand_6_out, and_7_out);
  nand nand_6 (nand_6_out, A14, A15);
  not not_26 (not_26_out, A12);
  and and_5 (and_5_out, x2, xA);
  LED u_rom (.in(ROM));
  and and_6 (ROM, and_4_out, nand_8_out);
  or or_23 (or_23_out, or_22_out, or_27_out);
  and and_7 (and_7_out, not_26_out, not_27_out);
  not not_27 (not_27_out, A13);
  nand nand_7 (nand_7_out, or_24_out, or_28_out);
  or or_24 (or_24_out, and_5_out, BSS);
  nand nand_8 (nand_8_out, and_8_out, not_28_out);
  and and_8 (and_8_out, and_9_out, BB);
  and and_9 (and_9_out, A13OR12, A15);
  or or_25 (or_25_out, nand_9_out, nand_10_out);
  nand nand_9 (nand_9_out, or_24_out, or_26_out);
  or or_26 (or_26_out, and_10_out, BSS);
  and and_10 (and_10_out, x1, x9);
  not not_28 (not_28_out, A14);
  and and_11 (and_11_out, RAMREAD, RW);
  LED A16 (.in(and_12_out));
  and and_12 (and_12_out, and_13_out, not_29_out);
  and and_13 (and_13_out, or_27_out, B2);
  or or_27 (or_27_out, and_11_out, and_14_out);
  and and_14 (and_14_out, RAMWRITE, not_30_out);
  J_K_Flip_Flop j_k_ff_1 (
    .J(FF), .K(NOWRITE), .clk(or_25_out), .Q(RAMWRITE), .Qn(NOWRITE), .reset(nand_7_out));  // open: preset
  nand nand_10 (nand_10_out, or_28_out, or_29_out);
  or or_28 (or_28_out, and_15_out, BSS);
  and and_15 (and_15_out, x8, x0);
  not not_29 (not_29_out, DXXX);
  not not_30 (not_30_out, RW);
  J_K_Flip_Flop j_k_ff_2 (
    .J(nand_9_out), .K(nand_10_out), .clk(CLK), .Q(ROMREAD), .Qn(RAMREAD));  // open: preset, reset
  nand nand_11 (nand_11_out, or_26_out, or_29_out);
  J_K_Flip_Flop j_k_ff_3 (.J(nand_11_out), .K(1'b0), .clk(CLK), .Q(FF), .reset(nand_7_out));  // open: Qn, preset
  or or_29 (or_29_out, and_16_out, BSS);
  and and_16 (and_16_out, xB, x3);
  LED GFX (.in(or_30_out));
  or or_30 (or_30_out, GFXSS, x0);
  nand nand_12 (PAGE1, or_31_out, PAGE2);
  LED u_PAGE1 (.in(or_31_out));
  or or_31 (or_31_out, GFXSS, x4);
  nand nand_13 (BB, C007, nand_17_out);
  nand nand_14 (GFXMODE, or_30_out, TXTMODE);
  LED TXT (.in(or_32_out));
  or or_32 (or_32_out, GFXSS, x1);
  nand nand_15 (PAGE2, PAGE1, or_33_out);
  nand nand_16 (TXTMODE, GFXMODE, or_32_out);
  LED u_PAGE2 (.in(or_33_out));
  or or_33 (or_33_out, GFXSS, x5);
  nand nand_17 (nand_17_out, BB, C006);
  nand nand_18 (B1, nand_19_out, B2);
  nand nand_19 (nand_19_out, not_31_out, A3);
  not not_31 (not_31_out, BSS);
  LED FULL (.in(or_34_out));
  or or_34 (or_34_out, GFXSS, x2);
  nand nand_20 (LORES, or_35_out, HIRES);
  LED u_LORES (.in(or_35_out));
  or or_35 (or_35_out, GFXSS, x6);
  LED u_KBD (.in(KBD));
  or or_36 (KBD, SS, LOW0);
  nand nand_21 (B2, B1, nand_24_out);
  not not_32 (not_32_out, A3);
  nand nand_22 (FULLMODE, or_34_out, MIXMODE);
  LED MIX (.in(or_37_out));
  or or_37 (or_37_out, GFXSS, x3);
  nand nand_23 (HIRES, LORES, or_38_out);
  nand nand_24 (nand_24_out, not_32_out, not_31_out);
  nand nand_25 (MIXMODE, FULLMODE, or_37_out);
  LED u_HIRES (.in(or_38_out));
  or or_38 (or_38_out, GFXSS, x7);
  not not_33 (not_33_out, VIDENABLE);
  DipSwitch #(.number(5)) dipswitch_2 (.sw1(PHI2), .sw2(VIDENABLE), .sw3(VIDBUS), .sw5(RW));  // open: sw4
  not not_34 (not_34_out, RW);
  not not_35 (not_35_out, PHI2);
  or or_39 (CS_ROM, not_33_out, ROM);
  or or_40 (CS_DEVICE, not_33_out, DEV);
  or or_41 (CS_CPUBUS, not_33_out, RAM);
  and and_17 (CS_RAM, RAM, VIDBUS);
  and and_18 (OE, VIDBUS, not_34_out);
  or or_42 (WE, RW, not_35_out);
endmodule
