// Logisim project apple2color.circ as structural Verilog: 1 circuit, main circuit main
module main (
);

  wire A_01_out, A_10_out, and_1_out, black_out, currbit, cyan_out, green_out, not_1_out, not_2_out,
       not_3_out, oddbit, orange_out, pallete, prevbit, violet_out, white_out, X_01_out, X_10_out, xor_1_out;

  not not_1 (not_1_out, currbit);
  not not_2 (not_2_out, prevbit);
  and A_01 (A_01_out, currbit, not_2_out);
  and white (white_out, currbit, prevbit);
  and black (black_out, not_1_out, not_2_out);
  and A_10 (A_10_out, not_1_out, prevbit);
  LED led_1 (.in(white_out));
  LED led_2 (.in(black_out));
  DipSwitch #(.number(4)) dipswitch_1 (.sw1(oddbit), .sw2(pallete), .sw3(prevbit), .sw4(currbit));
  xor xor_1 (xor_1_out, A_01_out, A_10_out);
  and and_1 (and_1_out, xor_1_out, oddbit);
  xor X_01 (X_01_out, A_01_out, and_1_out);
  xor X_10 (X_10_out, and_1_out, A_10_out);
  not not_3 (not_3_out, pallete);
  and orange (orange_out, X_01_out, pallete);
  and green (green_out, X_01_out, not_3_out);
  and violet (violet_out, not_3_out, X_10_out);
  and cyan (cyan_out, X_10_out, pallete);
  LED led_3 (.in(orange_out));
  LED led_4 (.in(green_out));
  LED led_5 (.in(violet_out));
  LED led_6 (.in(cyan_out));
endmodule
